# Fritzing sketch Final (saved by Fritzing 0.8.7b)
breadboards: 1

parts:
  Part3 = Arduino Nano (Rev3.0)
  LCD1 = LCD screen
  U1 = POT [package=trim_pot]
  J1 = Basic Servo
  R1 = Resistor [tolerance=±5% resistance=220 package=THT]
  R3 = Resistor [tolerance=±5% resistance=220 package=THT]
  Part4 = IR Receiver Breakout [package=PCB]
  LED4 = LED - 5mm [color="Green (570nm)" package="5 mm [THT]"]
  LED5 = LED - 5mm [color="Red (633nm)" package="5 mm [THT]"]

nets:
  GND: Part3.GND, LCD1.VSS, LCD1.R/W, LCD1.LED-, U1.A, J1.gnd, Part4.GND, LED4.anode, LED5.anode
  N1: Part3.D2, LCD1.RS
  N2: Part3.D3, LCD1.E
  N3: Part3.D4, LCD1.DB4
  N4: Part3.D5, LCD1.DB5
  N5: Part3.D6, LCD1.DB6
  N6: Part3.D7, LCD1.DB7
  N7: Part3.D9, R3.Pin_1
  N8: Part3.D10, R1.Pin_1
  N9: Part3.D11/MOSI, J1.pulse
  5V: Part3.5V, LCD1.VDD, LCD1.LED+, U1.S, J1.vcc, Part4.OUT
  N10: LCD1.V0, U1.E
  N11: R1.Pin_0, LED4.cathode
  N12: R3.Pin_0, LED5.cathode
